// Logisim project 4bits_counter.circ as structural Verilog: 1 circuit, main circuit main
module main (
  input  in_1,
  input  in_2,
  output [3:0] out_3
);

  wire and_1_out, and_2_out;

  J_K_Flip_Flop j_k_ff_1 (.J(in_1), .K(in_1), .clk(in_2), .Q(out_3[0]));  // open: Qn, preset, reset
  J_K_Flip_Flop j_k_ff_2 (.J(out_3[0]), .K(out_3[0]), .clk(in_2), .Q(out_3[1]));  // open: Qn, preset, reset
  and and_1 (and_1_out, out_3[1], out_3[0]);
  J_K_Flip_Flop j_k_ff_3 (.J(and_1_out), .K(and_1_out), .clk(in_2), .Q(out_3[2]));  // open: Qn, preset, reset
  and and_2 (and_2_out, out_3[1], out_3[0], out_3[2]);
  J_K_Flip_Flop j_k_ff_4 (.J(and_2_out), .K(and_2_out), .clk(in_2), .Q(out_3[3]));  // open: Qn, preset, reset
endmodule
