// Logisim project 4bits_counter_display.circ as structural Verilog: 1 circuit, main circuit main
module main (
  input  in_1
);

  wire and_1_out, and_2_out, and_3_out, bcd_to_7_segment_decoder_1_p1, bcd_to_7_segment_decoder_1_p2,
       bcd_to_7_segment_decoder_1_p3, bcd_to_7_segment_decoder_1_p4, bcd_to_7_segment_decoder_1_p6,
       bcd_to_7_segment_decoder_1_p7, bcd_to_7_segment_decoder_1_p8, clock_1_out, not_1_out;
  wire [3:0] j_k_ff_1_q;

  J_K_Flip_Flop j_k_ff_1 (.J(in_1), .K(in_1), .clk(clock_1_out), .Q(j_k_ff_1_q[0]));  // open: Qn, preset, reset
  Clock clock_1 (.out(clock_1_out));
  and and_1 (and_1_out, j_k_ff_1_q[0], not_1_out);
  J_K_Flip_Flop j_k_ff_2 (
    .J(and_1_out), .K(j_k_ff_1_q[0]), .clk(clock_1_out), .Q(j_k_ff_1_q[1]));  // open: Qn, preset, reset
  not not_1 (not_1_out, j_k_ff_1_q[3]);
  and and_2 (and_2_out, j_k_ff_1_q[0], j_k_ff_1_q[1]);
  J_K_Flip_Flop j_k_ff_3 (
    .J(and_2_out), .K(and_2_out), .clk(clock_1_out), .Q(j_k_ff_1_q[2]));  // open: Qn, preset, reset
  and and_3 (and_3_out, and_2_out, j_k_ff_1_q[2]);
  J_K_Flip_Flop j_k_ff_4 (
    .J(and_3_out), .K(j_k_ff_1_q[0]), .clk(clock_1_out), .Q(j_k_ff_1_q[3]));  // open: Qn, preset, reset
  // BCD_to_7_Segment_decoder bcd_to_7_segment_decoder_1: pin names not known; wires that end beside it: bcd_to_7_segment_decoder_1_p1, bcd_to_7_segment_decoder_1_p2, bcd_to_7_segment_decoder_1_p3, bcd_to_7_segment_decoder_1_p4, j_k_ff_1_q, bcd_to_7_segment_decoder_1_p6, bcd_to_7_segment_decoder_1_p7, bcd_to_7_segment_decoder_1_p8
  _7_Segment_Display u_7_segment_display_1 (
    .g(bcd_to_7_segment_decoder_1_p1), .f(bcd_to_7_segment_decoder_1_p3), .a(bcd_to_7_segment_decoder_1_p6),
    .b(bcd_to_7_segment_decoder_1_p8), .e(bcd_to_7_segment_decoder_1_p2), .d(bcd_to_7_segment_decoder_1_p4),
    .c(bcd_to_7_segment_decoder_1_p7));  // open: dp
endmodule
