// Logisim project 8bits_adder.circ as structural Verilog: 1 circuit, main circuit main
module main (
  input  [7:0] in_1,
  input  [7:0] in_2,
  output [7:0] out_3,
  output out_4
);

  wire and_1_out, and_2_out, and_3_out, and_4_out, and_5_out, and_6_out, and_7_out, and_8_out, and_9_out,
       and_10_out, and_11_out, and_12_out, and_13_out, and_14_out, and_15_out, or_1_out, or_2_out, or_3_out,
       or_4_out, or_5_out, or_6_out, xor_1_out, xor_2_out, xor_3_out, xor_4_out, xor_5_out, xor_6_out,
       xor_7_out;

  xor xor_1 (xor_1_out, in_1[1], in_2[1]);
  xor xor_2 (xor_2_out, in_1[2], in_2[2]);
  xor xor_3 (xor_3_out, in_1[3], in_2[3]);
  xor xor_4 (xor_4_out, in_1[4], in_2[4]);
  xor xor_5 (xor_5_out, in_1[5], in_2[5]);
  xor xor_6 (xor_6_out, in_1[6], in_2[6]);
  xor xor_7 (xor_7_out, in_1[7], in_2[7]);
  xor xor_8 (out_3[1], xor_1_out, and_15_out);
  and and_1 (and_1_out, xor_1_out, and_15_out);
  and and_2 (and_2_out, in_2[1], in_1[1]);
  xor xor_9 (out_3[2], xor_2_out, or_1_out);
  and and_3 (and_3_out, xor_2_out, or_1_out);
  and and_4 (and_4_out, in_2[2], in_1[2]);
  xor xor_10 (out_3[3], xor_3_out, or_2_out);
  and and_5 (and_5_out, xor_3_out, or_2_out);
  and and_6 (and_6_out, in_2[3], in_1[3]);
  xor xor_11 (out_3[4], xor_4_out, or_3_out);
  and and_7 (and_7_out, xor_4_out, or_3_out);
  and and_8 (and_8_out, in_2[4], in_1[4]);
  xor xor_12 (out_3[5], xor_5_out, or_4_out);
  and and_9 (and_9_out, xor_5_out, or_4_out);
  and and_10 (and_10_out, in_2[5], in_1[5]);
  xor xor_13 (out_3[6], xor_6_out, or_5_out);
  and and_11 (and_11_out, xor_6_out, or_5_out);
  and and_12 (and_12_out, in_2[6], in_1[6]);
  xor xor_14 (out_3[7], xor_7_out, or_6_out);
  and and_13 (and_13_out, xor_7_out, or_6_out);
  and and_14 (and_14_out, in_2[7], in_1[7]);
  xor xor_15 (out_3[0], in_1[0], in_2[0]);
  and and_15 (and_15_out, in_1[0], in_2[0]);
  or or_1 (or_1_out, and_1_out, and_2_out);
  or or_2 (or_2_out, and_3_out, and_4_out);
  or or_3 (or_3_out, and_5_out, and_6_out);
  or or_4 (or_4_out, and_7_out, and_8_out);
  or or_5 (or_5_out, and_9_out, and_10_out);
  or or_6 (or_6_out, and_11_out, and_12_out);
  or or_7 (out_4, and_13_out, and_14_out);
endmodule
