// Logisim project binary_comparator.circ as structural Verilog: 1 circuit, main circuit main
module main (
  input  in_1,
  input  in_2,
  input  [1:0] in_3,
  input  [1:0] in_4,
  input  [3:0] in_5,
  input  [3:0] in_6,
  output out_7,
  output out_8,
  output out_9,
  output out_10,
  output out_11,
  output out_12,
  output out_13,
  output out_14,
  output out_15
);

  wire and_3_out, and_4_out, and_5_out, and_6_out, and_7_out, and_8_out, and_9_out, and_10_out, and_11_out,
       and_12_out, and_13_out, and_16_out, not_1_out, not_2_out, not_3_out, not_4_out, not_5_out, not_6_out,
       not_7_out, not_8_out, not_9_out, not_10_out, not_11_out, not_12_out, xnor_2_out, xnor_3_out,
       xnor_4_out, xnor_5_out, xnor_6_out, xnor_7_out;

  not not_1 (not_1_out, in_2);
  not not_2 (not_2_out, in_1);
  and and_1 (out_7, in_1, not_1_out);
  xnor xnor_1 (out_8, in_1, in_2);
  and and_2 (out_9, in_2, not_2_out);
  xnor xnor_2 (xnor_2_out, in_5[0], in_6[0]);
  xnor xnor_3 (xnor_3_out, in_5[1], in_6[1]);
  xnor xnor_4 (xnor_4_out, in_5[2], in_6[2]);
  xnor xnor_5 (xnor_5_out, in_5[3], in_6[3]);
  and and_3 (and_3_out, in_5[0], not_3_out);
  not not_3 (not_3_out, in_6[0]);
  and and_4 (and_4_out, in_5[1], not_4_out);
  not not_4 (not_4_out, in_6[1]);
  and and_5 (and_5_out, in_5[2], not_5_out);
  not not_5 (not_5_out, in_6[2]);
  and and_6 (and_6_out, in_5[3], not_6_out);
  not not_6 (not_6_out, in_6[3]);
  xnor xnor_6 (xnor_6_out, in_3[0], in_4[0]);
  xnor xnor_7 (xnor_7_out, in_3[1], in_4[1]);
  and and_7 (and_7_out, in_3[0], not_7_out);
  not not_7 (not_7_out, in_4[0]);
  and and_8 (and_8_out, in_3[1], not_8_out);
  not not_8 (not_8_out, in_4[1]);
  and and_9 (and_9_out, xnor_2_out, xnor_3_out);
  and and_10 (and_10_out, xnor_4_out, xnor_3_out, xnor_5_out, and_3_out);
  and and_11 (and_11_out, xnor_7_out, and_7_out);
  and and_12 (and_12_out, and_9_out, xnor_4_out);
  and and_13 (and_13_out, xnor_4_out, xnor_5_out, and_4_out);
  and and_14 (out_10, xnor_6_out, xnor_7_out);
  or or_1 (out_12, and_11_out, and_8_out);
  and and_15 (out_13, and_12_out, xnor_5_out);
  and and_16 (and_16_out, xnor_5_out, and_5_out);
  or or_2 (out_15, and_10_out, and_13_out, and_16_out, and_6_out);
  not not_9 (not_9_out, out_10);
  not not_10 (not_10_out, out_12);
  not not_11 (not_11_out, out_13);
  not not_12 (not_12_out, out_15);
  and and_17 (out_11, not_9_out, not_10_out);
  and and_18 (out_14, not_11_out, not_12_out);
endmodule
