// Logisim project calc_v0.1.circ as structural Verilog: 6 circuits, main circuit main
module main (
  input  substract,
  input  [3:0] num1,
  input  [3:0] num2,
  input  operate_with_result
);

  wire binary2display_1_a, binary2display_1_b, binary2display_1_c, binary2display_1_d, binary2display_1_e,
       binary2display_1_f, binary2display_1_g, equal_out, or_4_out, sum_sub_1_out_5;
  wire [3:0] and_1_out, and_2_out, and_3_out, and_4_out, and_5_out, and_6_out, and_7_out, and_9_out,
       and_10_out, d_ff_5_q, not_1_out, not_2_out, not_3_out, not_4_out, or_1_out, or_2_out, or_3_out,
       or_5_out, sum_sub_1_out_4;
  wire [3:3] and_8_out;

  Button equal (.out(equal_out));
  assign and_1_out = {4{substract}} & {4{operate_with_result}};  // AND_Gate and_1, 4 bits wide
  assign and_2_out = num2 & not_1_out;  // AND_Gate and_2, 4 bits wide
  assign not_1_out = ~{4{operate_with_result}};  // NOT_Gate not_1, 4 bits wide
  assign and_3_out = num1 & not_2_out;  // AND_Gate and_3, 4 bits wide
  assign not_2_out = ~and_1_out;  // NOT_Gate not_2, 4 bits wide
  assign and_4_out = or_1_out & and_1_out;  // AND_Gate and_4, 4 bits wide
  assign and_5_out = num1 & and_1_out;  // AND_Gate and_5, 4 bits wide
  assign and_6_out = or_1_out & not_3_out;  // AND_Gate and_6, 4 bits wide
  assign not_3_out = ~and_1_out;  // NOT_Gate not_3, 4 bits wide
  assign or_1_out = and_2_out | and_7_out;  // OR_Gate or_1, 4 bits wide
  assign and_7_out = d_ff_5_q & {4{operate_with_result}};  // AND_Gate and_7, 4 bits wide
  assign or_2_out = and_3_out | and_4_out;  // OR_Gate or_2, 4 bits wide
  assign or_3_out = and_5_out | and_6_out;  // OR_Gate or_3, 4 bits wide
  and and_8 (and_8_out[3], d_ff_5_q[3], or_4_out);
  or or_4 (or_4_out, d_ff_5_q[2], d_ff_5_q[1]);
  sum_sub sum_sub_1 (
    .in_1(substract), .in_2(or_2_out), .in_3(or_3_out), .out_4(sum_sub_1_out_4), .out_5(sum_sub_1_out_5));
  D_Flip_Flop d_ff_1 (.D(sum_sub_1_out_5), .clk(equal_out));  // open: Q, Qn, preset, reset
  assign and_9_out = d_ff_5_q & not_4_out;  // AND_Gate and_9, 4 bits wide
  assign not_4_out = ~{4{and_8_out[3]}};  // NOT_Gate not_4, 4 bits wide
  assign and_10_out = 4'b1001 & {4{and_8_out[3]}};  // AND_Gate and_10, 4 bits wide
  D_Flip_Flop d_ff_2 (.D(sum_sub_1_out_4[3]), .clk(equal_out), .Q(d_ff_5_q[3]));  // open: Qn, preset, reset
  assign or_5_out = and_9_out | and_10_out;  // OR_Gate or_5, 4 bits wide
  D_Flip_Flop d_ff_3 (.D(sum_sub_1_out_4[2]), .clk(equal_out), .Q(d_ff_5_q[2]));  // open: Qn, preset, reset
  D_Flip_Flop d_ff_4 (.D(sum_sub_1_out_4[1]), .clk(equal_out), .Q(d_ff_5_q[1]));  // open: Qn, preset, reset
  D_Flip_Flop d_ff_5 (.D(sum_sub_1_out_4[0]), .clk(equal_out), .Q(d_ff_5_q[0]));  // open: Qn, preset, reset
  binary2display binary2display_1 (
    .in_1(or_5_out), .b(binary2display_1_b), .a(binary2display_1_a), .f(binary2display_1_f),
    .g(binary2display_1_g), .e(binary2display_1_e), .d(binary2display_1_d), .c(binary2display_1_c));
  _7_Segment_Display u_7_segment_display_1 (
    .f(and_8_out[3]), .a(and_8_out[3]), .e(and_8_out[3]), .d(and_8_out[3]));  // open: g, b, c, dp
  _7_Segment_Display u_7_segment_display_2 (
    .g(binary2display_1_g), .f(binary2display_1_f), .a(binary2display_1_a), .b(binary2display_1_b),
    .e(binary2display_1_e), .d(binary2display_1_d), .c(binary2display_1_c));  // open: dp
endmodule

module sum_sub (
  input  in_1,
  input  [3:0] in_2,
  input  [3:0] in_3,
  output [3:0] out_4,
  output out_5
);

  wire full_adder_1_out_5, full_adder_2_out_5, full_adder_3_out_5, full_adder_4_out_5, inversor_1_out_6,
       inversor_1_out_7, inversor_1_out_8, inversor_1_out_9;

  inversor inversor_1 (
    .in_1(in_3[0]), .in_2(in_3[1]), .in_3(in_3[2]), .in_4(in_3[3]), .in_5(in_1), .out_6(inversor_1_out_6),
    .out_7(inversor_1_out_7), .out_8(inversor_1_out_8), .out_9(inversor_1_out_9));
  full_adder full_adder_1 (
    .in_1(in_1), .in_2(in_2[0]), .in_3(inversor_1_out_6), .out_4(out_4[0]), .out_5(full_adder_1_out_5));
  full_adder full_adder_2 (
    .in_1(full_adder_1_out_5), .in_2(in_2[1]), .in_3(inversor_1_out_7), .out_4(out_4[1]),
    .out_5(full_adder_2_out_5));
  full_adder full_adder_3 (
    .in_1(full_adder_2_out_5), .in_2(in_2[2]), .in_3(inversor_1_out_8), .out_4(out_4[2]),
    .out_5(full_adder_3_out_5));
  full_adder full_adder_4 (
    .in_1(full_adder_3_out_5), .in_2(in_2[3]), .in_3(inversor_1_out_9), .out_4(out_4[3]),
    .out_5(full_adder_4_out_5));
  xor xor_1 (out_5, full_adder_4_out_5, in_1);
endmodule

module half_adder (
  input  in_1,
  input  in_2,
  output out_3,
  output out_4
);

  xor xor_1 (out_3, in_1, in_2);
  and and_1 (out_4, in_1, in_2);
endmodule

module full_adder (
  input  in_1,
  input  in_2,
  input  in_3,
  output out_4,
  output out_5
);

  wire half_adder_1_out_3, half_adder_1_out_4, half_adder_2_out_4;

  half_adder half_adder_1 (.in_1(in_2), .in_2(in_3), .out_3(half_adder_1_out_3), .out_4(half_adder_1_out_4));
  half_adder half_adder_2 (.in_1(in_1), .in_2(half_adder_1_out_3), .out_3(out_4), .out_4(half_adder_2_out_4));
  or or_1 (out_5, half_adder_2_out_4, half_adder_1_out_4);
endmodule

module inversor (
  input  in_1,
  input  in_2,
  input  in_3,
  input  in_4,
  input  in_5,
  output out_6,
  output out_7,
  output out_8,
  output out_9
);

  xor xor_1 (out_6, in_1, in_5);
  xor xor_2 (out_7, in_2, in_5);
  xor xor_3 (out_8, in_3, in_5);
  xor xor_4 (out_9, in_4, in_5);
endmodule

module binary2display (
  input  [3:0] in_1,
  output b,
  output a,
  output f,
  output g,
  output e,
  output d,
  output c
);

  wire and_1_out, and_2_out, and_3_out, and_4_out, and_5_out, and_6_out, and_7_out, and_8_out, nand_1_out,
       nand_2_out, nand_3_out, nor_1_out, nor_2_out, nor_3_out, nor_4_out, nor_5_out, not_1_out, not_2_out,
       not_3_out, not_4_out, not_5_out, not_6_out;

  not not_1 (not_1_out, in_1[2]);
  and and_1 (and_1_out, in_1[1], in_1[0]);
  not not_2 (not_2_out, in_1[2]);
  not not_3 (not_3_out, in_1[0]);
  not not_4 (not_4_out, in_1[1]);
  or or_1 (c, in_1[2], not_4_out, in_1[0]);
  nor nor_1 (nor_1_out, in_1[1], in_1[0]);
  or or_2 (b, not_1_out, nor_1_out, and_1_out);
  nor nor_2 (nor_2_out, in_1[2], in_1[0]);
  and and_2 (and_2_out, in_1[2], in_1[0]);
  and and_3 (and_3_out, in_1[2], nand_1_out);
  nand nand_1 (nand_1_out, in_1[1], in_1[0]);
  nor nor_3 (nor_3_out, in_1[1], in_1[0]);
  and and_4 (and_4_out, in_1[2], nand_2_out);
  nand nand_2 (nand_2_out, in_1[1], in_1[0]);
  and and_5 (and_5_out, not_2_out, in_1[1]);
  nor nor_4 (nor_4_out, in_1[2], in_1[0]);
  and and_6 (and_6_out, not_3_out, in_1[1]);
  nor nor_5 (nor_5_out, in_1[2], in_1[0]);
  not not_5 (not_5_out, in_1[1]);
  nand nand_3 (nand_3_out, in_1[2], in_1[0]);
  not not_6 (not_6_out, nand_3_out);
  or or_3 (a, nor_2_out, in_1[1], in_1[3], and_2_out);
  or or_4 (f, in_1[3], and_3_out, nor_3_out);
  or or_5 (g, in_1[3], and_4_out, and_5_out);
  or or_6 (e, nor_4_out, and_6_out);
  and and_7 (and_7_out, not_5_out, not_6_out);
  and and_8 (and_8_out, in_1[1], nand_3_out);
  or or_7 (d, in_1[3], nor_5_out, and_7_out, and_8_out);
endmodule
