// Logisim project calc_v0.1_proto.circ as structural Verilog: 5 circuits, main circuit main
module main (
  input  sum_sub_selector,
  input  [3:0] num_3,
  input  [3:0] num_2,
  input  num_2_result_selector,
  output [3:0] result
);

  wire equal_out, sum_sub_1_out_5;
  wire [3:0] and_1_out, and_2_out, and_3_out, and_4_out, and_5_out, and_6_out, and_7_out, not_1_out,
       not_2_out, not_3_out, or_1_out, or_2_out, or_3_out, sum_sub_1_out_4;

  Button equal (.out(equal_out));
  assign and_1_out = {4{sum_sub_selector}} & {4{num_2_result_selector}};  // AND_Gate and_1, 4 bits wide
  assign not_1_out = ~and_1_out;  // NOT_Gate not_1, 4 bits wide
  assign not_2_out = ~and_1_out;  // NOT_Gate not_2, 4 bits wide
  assign or_1_out = and_2_out | and_3_out;  // OR_Gate or_1, 4 bits wide
  assign and_2_out = num_2 & not_3_out;  // AND_Gate and_2, 4 bits wide
  assign and_3_out = result & {4{num_2_result_selector}};  // AND_Gate and_3, 4 bits wide
  assign not_3_out = ~{4{num_2_result_selector}};  // NOT_Gate not_3, 4 bits wide
  assign and_4_out = num_3 & not_1_out;  // AND_Gate and_4, 4 bits wide
  assign or_2_out = and_4_out | and_5_out;  // OR_Gate or_2, 4 bits wide
  assign and_5_out = or_1_out & and_1_out;  // AND_Gate and_5, 4 bits wide
  assign and_6_out = num_3 & and_1_out;  // AND_Gate and_6, 4 bits wide
  assign or_3_out = and_6_out | and_7_out;  // OR_Gate or_3, 4 bits wide
  assign and_7_out = or_1_out & not_2_out;  // AND_Gate and_7, 4 bits wide
  sum_sub sum_sub_1 (
    .in_1(sum_sub_selector), .in_2(or_2_out), .in_3(or_3_out), .out_4(sum_sub_1_out_4),
    .out_5(sum_sub_1_out_5));
  D_Flip_Flop d_ff_1 (.D(sum_sub_1_out_5), .clk(equal_out));  // open: Q, Qn, preset, reset
  D_Flip_Flop d_ff_2 (.D(sum_sub_1_out_4[3]), .clk(equal_out), .Q(result[3]));  // open: Qn, preset, reset
  D_Flip_Flop d_ff_3 (.D(sum_sub_1_out_4[2]), .clk(equal_out), .Q(result[2]));  // open: Qn, preset, reset
  D_Flip_Flop d_ff_4 (.D(sum_sub_1_out_4[1]), .clk(equal_out), .Q(result[1]));  // open: Qn, preset, reset
  D_Flip_Flop d_ff_5 (.D(sum_sub_1_out_4[0]), .clk(equal_out), .Q(result[0]));  // open: Qn, preset, reset
endmodule

module sum_sub (
  input  in_1,
  input  [3:0] in_2,
  input  [3:0] in_3,
  output [3:0] out_4,
  output out_5
);

  wire full_adder_1_out_5, full_adder_2_out_5, full_adder_3_out_5, full_adder_4_out_5, inversor_1_out_6,
       inversor_1_out_7, inversor_1_out_8, inversor_1_out_9;

  inversor inversor_1 (
    .in_1(in_3[0]), .in_2(in_3[1]), .in_3(in_3[2]), .in_4(in_3[3]), .in_5(in_1), .out_6(inversor_1_out_6),
    .out_7(inversor_1_out_7), .out_8(inversor_1_out_8), .out_9(inversor_1_out_9));
  full_adder full_adder_1 (
    .in_1(in_1), .in_2(in_2[0]), .in_3(inversor_1_out_6), .out_4(out_4[0]), .out_5(full_adder_1_out_5));
  full_adder full_adder_2 (
    .in_1(full_adder_1_out_5), .in_2(in_2[1]), .in_3(inversor_1_out_7), .out_4(out_4[1]),
    .out_5(full_adder_2_out_5));
  full_adder full_adder_3 (
    .in_1(full_adder_2_out_5), .in_2(in_2[2]), .in_3(inversor_1_out_8), .out_4(out_4[2]),
    .out_5(full_adder_3_out_5));
  full_adder full_adder_4 (
    .in_1(full_adder_3_out_5), .in_2(in_2[3]), .in_3(inversor_1_out_9), .out_4(out_4[3]),
    .out_5(full_adder_4_out_5));
  xor xor_1 (out_5, full_adder_4_out_5, in_1);
endmodule

module half_adder (
  input  in_1,
  input  in_2,
  output out_3,
  output out_4
);

  xor xor_1 (out_3, in_1, in_2);
  and and_1 (out_4, in_1, in_2);
endmodule

module full_adder (
  input  in_1,
  input  in_2,
  input  in_3,
  output out_4,
  output out_5
);

  wire half_adder_1_out_3, half_adder_1_out_4, half_adder_2_out_4;

  half_adder half_adder_1 (.in_1(in_2), .in_2(in_3), .out_3(half_adder_1_out_3), .out_4(half_adder_1_out_4));
  half_adder half_adder_2 (.in_1(in_1), .in_2(half_adder_1_out_3), .out_3(out_4), .out_4(half_adder_2_out_4));
  or or_1 (out_5, half_adder_2_out_4, half_adder_1_out_4);
endmodule

module inversor (
  input  in_1,
  input  in_2,
  input  in_3,
  input  in_4,
  input  in_5,
  output out_6,
  output out_7,
  output out_8,
  output out_9
);

  xor xor_1 (out_6, in_1, in_5);
  xor xor_2 (out_7, in_2, in_5);
  xor xor_3 (out_8, in_3, in_5);
  xor xor_4 (out_9, in_4, in_5);
endmodule
