// Logisim project multiplexers_demultiplexers.circ as structural Verilog: 1 circuit, main circuit main
module main (
  input  in_1,
  input  in_2,
  input  in_3,
  input  in_4,
  input  in_5,
  input  in_6,
  input  in_7,
  input  in_8,
  input  in_9,
  input  in_10,
  input  [1:0] in_11,
  input  [1:0] in_12,
  output out_13,
  output out_14,
  output out_15,
  output out_16,
  output out_17,
  output out_18,
  output out_19,
  output out_20
);

  wire and_1_out, and_2_out, and_5_out, and_6_out, and_7_out, and_8_out, and_9_out, and_10_out, and_11_out,
       and_12_out, nand_1_out, nand_2_out, nor_1_out, nor_2_out, not_1_out, not_2_out;

  not not_1 (not_1_out, in_6);
  not not_2 (not_2_out, in_10);
  and and_1 (and_1_out, in_1, not_1_out);
  and and_2 (and_2_out, in_2, in_6);
  and and_3 (out_19, not_2_out, in_9);
  and and_4 (out_20, in_9, in_10);
  or or_1 (out_13, and_1_out, and_2_out);
  and and_5 (and_5_out, in_11[1], nand_1_out);
  nor nor_1 (nor_1_out, in_11[1], in_11[0]);
  and and_6 (and_6_out, nand_1_out, in_11[0]);
  nand nand_1 (nand_1_out, in_11[0], in_11[1]);
  and and_7 (and_7_out, in_3, nor_1_out);
  and and_8 (and_8_out, in_4, and_6_out);
  and and_9 (and_9_out, and_5_out, in_7);
  and and_10 (and_10_out, in_11[1], in_11[0], in_8);
  or or_2 (out_16, and_7_out, and_8_out, and_9_out, and_10_out);
  and and_11 (and_11_out, in_12[1], nand_2_out);
  nor nor_2 (nor_2_out, in_12[1], in_12[0]);
  and and_12 (and_12_out, nand_2_out, in_12[0]);
  nand nand_2 (nand_2_out, in_12[1], in_12[0]);
  and and_13 (out_14, in_5, nor_2_out);
  and and_14 (out_15, in_5, and_12_out);
  and and_15 (out_17, and_11_out, in_5);
  and and_16 (out_18, in_12[1], in_12[0], in_5);
endmodule
