// Logisim project ram8x8.circ as structural Verilog: 4 circuits, main circuit main
module cell_8x1 (
  input  addr_1,
  input  addr_0,
  input  addr_2,
  input  write,
  input  data_in,
  output data_out
);

  wire d_ff_1_q, d_ff_2_q, d_ff_3_q, d_ff_4_q, d_ff_5_q, d_ff_6_q, d_ff_7_q, d_ff_8_q, decoder_3_8_1_o_0,
       decoder_3_8_1_o_1, decoder_3_8_1_o_2, decoder_3_8_1_o_3, decoder_3_8_1_o_4, decoder_3_8_1_o_5,
       decoder_3_8_1_o_6, decoder_3_8_1_o_7;

  D_Flip_Flop d_ff_1 (.D(data_in), .clk(decoder_3_8_1_o_7), .Q(d_ff_1_q));  // open: Qn, preset, reset
  D_Flip_Flop d_ff_2 (.D(data_in), .clk(decoder_3_8_1_o_6), .Q(d_ff_2_q));  // open: Qn, preset, reset
  D_Flip_Flop d_ff_3 (.D(data_in), .clk(decoder_3_8_1_o_5), .Q(d_ff_3_q));  // open: Qn, preset, reset
  D_Flip_Flop d_ff_4 (.D(data_in), .clk(decoder_3_8_1_o_4), .Q(d_ff_4_q));  // open: Qn, preset, reset
  D_Flip_Flop d_ff_5 (.D(data_in), .clk(decoder_3_8_1_o_3), .Q(d_ff_5_q));  // open: Qn, preset, reset
  D_Flip_Flop d_ff_6 (.D(data_in), .clk(decoder_3_8_1_o_2), .Q(d_ff_6_q));  // open: Qn, preset, reset
  D_Flip_Flop d_ff_7 (.D(data_in), .clk(decoder_3_8_1_o_1), .Q(d_ff_7_q));  // open: Qn, preset, reset
  decoder_3_8 decoder_3_8_1 (
    .write(write), .sel_2(addr_2), .sel_1(addr_1), .sel_0(addr_0), .o_0(decoder_3_8_1_o_0),
    .o_2(decoder_3_8_1_o_2), .o_4(decoder_3_8_1_o_4), .o_6(decoder_3_8_1_o_6), .o_1(decoder_3_8_1_o_1),
    .o_3(decoder_3_8_1_o_3), .o_5(decoder_3_8_1_o_5), .o_7(decoder_3_8_1_o_7));
  D_Flip_Flop d_ff_8 (.D(data_in), .clk(decoder_3_8_1_o_0), .Q(d_ff_8_q));  // open: Qn, preset, reset
  selector_8_1 selector_8_1_1 (
    .sel_1(addr_1), .sel_0(addr_2), .sel_2(addr_0), .d_0(d_ff_8_q), .d_1(d_ff_7_q), .d_2(d_ff_6_q),
    .d_3(d_ff_5_q), .d_4(d_ff_4_q), .d_5(d_ff_3_q), .d_6(d_ff_2_q), .d_7(d_ff_1_q), .ouput(data_out));
endmodule

module selector_8_1 (
  input  d_0,
  input  d_2,
  input  d_4,
  input  d_6,
  input  d_1,
  input  d_3,
  input  d_5,
  input  d_7,
  input  sel_0,
  input  sel_1,
  input  sel_2,
  output ouput
);

  Multiplexer #(.select(3)) multiplexer_1 (
    .in0(d_0), .in1(d_1), .in2(d_2), .in3(d_3), .in4(d_4), .in5(d_5), .in6(d_6), .in7(d_7), .out(ouput));  // open: sel
endmodule

module decoder_3_8 (
  input  write,
  input  sel_2,
  input  sel_0,
  input  sel_1,
  output o_0,
  output o_1,
  output o_2,
  output o_3,
  output o_4,
  output o_5,
  output o_6,
  output o_7
);

  Demultiplexer #(.select(3)) demultiplexer_1 (
    .out0(o_0), .out1(o_1), .out2(o_2), .out3(o_3), .out4(o_4), .out5(o_5), .out6(o_6), .out7(o_7),
    .in(write), .sel({sel_2, sel_1, sel_0}));
endmodule

module main (
);

  wire cell_8x1_1_data_out, cell_8x1_2_data_out, cell_8x1_3_data_out, cell_8x1_4_data_out,
       cell_8x1_5_data_out, cell_8x1_6_data_out, cell_8x1_7_data_out, cell_8x1_8_data_out, undriven,
       undriven_2, undriven_3, undriven_4, undriven_5;

  cell_8x1 cell_8x1_1 (
    .addr_0(undriven), .addr_1(undriven_2), .addr_2(undriven_3), .write(undriven_4), .data_in(undriven_5),
    .data_out(cell_8x1_1_data_out));
  cell_8x1 cell_8x1_2 (
    .addr_0(undriven), .addr_1(undriven_2), .addr_2(undriven_3), .write(undriven_4), .data_in(undriven_5),
    .data_out(cell_8x1_2_data_out));
  cell_8x1 cell_8x1_3 (
    .addr_0(undriven), .addr_1(undriven_2), .addr_2(undriven_3), .write(undriven_4), .data_in(undriven_5),
    .data_out(cell_8x1_3_data_out));
  cell_8x1 cell_8x1_4 (
    .addr_0(undriven), .addr_1(undriven_2), .addr_2(undriven_3), .write(undriven_4), .data_in(undriven_5),
    .data_out(cell_8x1_4_data_out));
  cell_8x1 cell_8x1_5 (
    .addr_0(undriven), .addr_1(undriven_2), .addr_2(undriven_3), .write(undriven_4), .data_in(undriven_5),
    .data_out(cell_8x1_5_data_out));
  cell_8x1 cell_8x1_6 (
    .addr_0(undriven), .addr_1(undriven_2), .addr_2(undriven_3), .write(undriven_4), .data_in(undriven_5),
    .data_out(cell_8x1_6_data_out));
  cell_8x1 cell_8x1_7 (
    .addr_0(undriven), .addr_1(undriven_2), .addr_2(undriven_3), .write(undriven_4), .data_in(undriven_5),
    .data_out(cell_8x1_7_data_out));
  cell_8x1 cell_8x1_8 (
    .addr_0(undriven), .addr_1(undriven_2), .addr_2(undriven_3), .write(undriven_4), .data_in(undriven_5),
    .data_out(cell_8x1_8_data_out));
endmodule
